// Logisim project CPU.circ as structural Verilog: 1 circuit, main circuit Ida CPU
// CPU
module Ida_CPU (
  input  [31:0] Instruction,
  input  Clock,
  output [23:0] Mem_Data,
  output [23:0] Mem_Address,
  output Mem_Write,
  output [23:0] Next_PC,
  output [23:0] r00,
  output [23:0] r01,
  output [23:0] r02,
  output [23:0] r03,
  output [23:0] r04,
  output [23:0] r05,
  output [23:0] r06,
  output [23:0] r07,
  output [23:0] r08,
  output [23:0] r09,
  output [23:0] r10,
  output [23:0] r11,
  output [23:0] r12,
  output [23:0] r13,
  output [23:0] r14,
  output [23:0] r15
);

  wire CMP, comparator_1_lt, comparator_2_eq, comparator_4_eq, comparator_5_eq, comparator_6_eq,
       comparator_7_eq, comparator_8_eq, comparator_9_eq, comparator_10_eq, CQBool, IMM, jump, JUMPLINK,
       link, not_1_out, not_2_out, not_3_out, or_1_out, or_2_out, or_3_out, or_6_out, RegWrite;
  wire [0:0] TYPE;
  wire [2:0] bit_extender_4_out, CQ, cr, multiplexer_8_out;
  wire [3:0] multiplexer_3_out, multiplexer_4_out, OP, zeroRI;
  wire [23:0] adder_1_out, bit_extender_2_out, bit_extender_3_out, demultiplexer_1_out1,
       demultiplexer_2_out1, demultiplexer_3_out1, ida_alu_1_alu_result, ida_register_file_1_reg_1_value,
       ida_register_file_1_reg_2_value, IMM_VAL, multiplexer_5_out, multiplexer_6_out, multiplexer_9_out,
       multiplexer_10_out, oneA1RI, ram_2_data;
  wire [31:0] multiplexer_1_out, testing;

  // Probe on Instruction
  // Probe on Clock
  // Probe on r00
  // Probe on r01
  // Probe on r02
  // Probe on r03
  // Probe on r04
  // Probe on r05
  // Probe on r06
  // Probe on r07
  // Probe on Mem_Data
  // Probe on Mem_Address
  // Probe on Mem_Write
  // Probe on Next_PC
  // Probe on r08
  // Probe on r09
  // Probe on r10
  // Probe on r11
  // Probe on r12
  // Probe on r13
  // Probe on r14
  // Probe on r15
  Bit_Extender #(.in_width(32), .out_width(4)) bit_extender_1 (.in({OP, CQ, IMM, oneA1RI}), .out(zeroRI));
  Multiplexer #(.width(32), .enable("false")) multiplexer_1 (
    .in0(Instruction), .in1({32{1'b0}}), .out(multiplexer_1_out), .sel(jump));
  // Probe on multiplexer_1_out
  Register #(.width(32)) register_1 (.D(multiplexer_1_out), .Q({OP, CQ, IMM, oneA1RI}), .clk(Clock));  // open: en, clr
  not not_1 (not_1_out, cr[1]);
  Comparator #(.width(4), .mode("unsigned")) comparator_1 (
    .a(OP), .b(4'b1011), .eq(Mem_Write), .lt(comparator_1_lt));  // open: gt
  Comparator #(.width(4), .mode("unsigned")) comparator_2 (.a(OP), .b(4'b1110), .eq(comparator_2_eq));  // open: gt, lt
  or or_1 (or_1_out, cr[2], cr[1]);
  or or_2 (or_2_out, cr[0], cr[1]);
  or or_3 (or_3_out, comparator_1_lt, comparator_2_eq);
  Clock clock_1 (.out(Clock));
  // Probe on CQ
  Multiplexer #(.select(3), .enable("false")) multiplexer_2 (
    .in0(1'b0), .in1(or_1_out), .in2(cr[0]), .in3(not_1_out), .in4(cr[1]), .in5(or_2_out), .in6(cr[2]),
    .in7(1'b1), .out(CQBool), .sel(CQ));
  // Probe on CQBool
  and and_1 (RegWrite, or_3_out, CQBool);
  RAM #(.addrWidth(24), .dataWidth(32)) ram_1 (.addr(Next_PC), .data(testing), .clk(Clock));  // open: sel, ld, clr
  // Probe on testing
  Multiplexer #(.width(4), .enable("false")) multiplexer_3 (
    .in0(oneA1RI[19:16]), .in1(oneA1RI[23:20]), .out(multiplexer_3_out), .sel(CMP));
  Multiplexer #(.width(4), .enable("false")) multiplexer_4 (
    .in0(oneA1RI[23:20]), .in1(4'b0010), .out(multiplexer_4_out), .sel(link));
  // Probe on multiplexer_4_out
  Multiplexer #(.width(24), .enable("false")) multiplexer_5 (
    .in0(multiplexer_10_out), .in1(IMM_VAL), .out(multiplexer_5_out), .sel(link));
  // Probe on multiplexer_5_out
  Ida_Register_File ida_register_file_1 (
    .Read_Reg_1(multiplexer_3_out), .Read_Reg_2(zeroRI), .Write_Reg(multiplexer_4_out),
    .Write_Value(multiplexer_5_out), .Reg_1_Value(ida_register_file_1_reg_1_value),
    .Reg_2_Value(ida_register_file_1_reg_2_value), .Reg_Write(RegWrite), .Clock(Clock), .r00(r00), .r01(r01),
    .r02(r02), .r03(r03), .r04(r04), .r05(r05), .r06(r06), .r07(r07), .r08(r08), .r09(r09), .r10(r10),
    .r11(r11), .r12(r12), .r13(r13), .r14(r14), .r15(r15), .Reg_3_Value(Mem_Data));
  assign bit_extender_2_out = {{8{oneA1RI[15]}}, oneA1RI[15:0]};  // Bit_Extender bit_extender_2
  assign bit_extender_3_out = {{4{oneA1RI[19]}}, oneA1RI[19:0]};  // Bit_Extender bit_extender_3
  Comparator #(.width(4), .mode("unsigned")) comparator_3 (.a(OP), .b(4'b1100), .lt(TYPE[0]));  // open: gt, eq
  Comparator #(.width(4), .mode("unsigned")) comparator_4 (.a(OP), .b(4'b1100), .eq(comparator_4_eq));  // open: gt, lt
  Comparator #(.width(4), .mode("unsigned")) comparator_5 (.a(OP), .b(4'b1101), .eq(comparator_5_eq));  // open: gt, lt
  Comparator #(.width(4), .mode("unsigned")) comparator_6 (.a(OP), .b(4'b1110), .eq(comparator_6_eq));  // open: gt, lt
  Comparator #(.width(4), .mode("unsigned")) comparator_7 (.a(OP), .b(4'b1111), .eq(comparator_7_eq));  // open: gt, lt
  // Probe on Mem_Data
  Multiplexer #(.select(3), .width(24), .enable("false")) multiplexer_6 (
    .in1(bit_extender_2_out), .in2(bit_extender_3_out), .in4(oneA1RI), .out(multiplexer_6_out),
    .sel({JUMPLINK, CMP, TYPE[0]}));  // open: in0, in3, in5, in6, in7
  // Probe on multiplexer_6_out
  or or_4 (CMP, comparator_4_eq, comparator_5_eq);
  or or_5 (JUMPLINK, comparator_6_eq, comparator_7_eq);
  Demultiplexer #(.width(24), .enable("false")) demultiplexer_1 (
    .out1(demultiplexer_1_out1), .in(ida_register_file_1_reg_1_value), .sel(CQBool));  // open: out0
  Demultiplexer #(.width(24), .enable("false")) demultiplexer_2 (
    .out1(demultiplexer_2_out1), .in(IMM_VAL), .sel(CQBool));  // open: out0
  Multiplexer #(.width(24), .enable("false")) multiplexer_7 (
    .in0(ida_register_file_1_reg_2_value), .in1(multiplexer_6_out), .out(IMM_VAL), .sel(IMM));
  // Probe on demultiplexer_2_out1
  // Probe on ida_alu_1_alu_result
  Demultiplexer #(.width(24), .enable("false")) demultiplexer_3 (
    .out0(Mem_Address), .out1(demultiplexer_3_out1), .in(ida_alu_1_alu_result), .sel(CMP));
  Ida_ALU ida_alu_1 (
    .ALU_Source_1(demultiplexer_1_out1), .ALU_Source_2(demultiplexer_2_out1), .Operation(OP),
    .ALU_Result(ida_alu_1_alu_result));
  Multiplexer #(.width(3), .enable("false")) multiplexer_8 (
    .in1(bit_extender_4_out), .out(multiplexer_8_out), .sel(CMP));  // open: in0
  // Probe on multiplexer_8_out
  Comparator #(.width(4), .mode("unsigned")) comparator_8 (.a(OP), .b(4'b1111), .eq(comparator_8_eq));  // open: gt, lt
  Comparator #(.width(4), .mode("unsigned")) comparator_9 (.a(OP), .b(4'b1110), .eq(comparator_9_eq));  // open: gt, lt
  // Probe on Mem_Address
  Bit_Extender #(.in_width(24), .out_width(3)) bit_extender_4 (.in(demultiplexer_3_out1), .out(bit_extender_4_out));
  Register #(.width(3)) register_2 (.D(multiplexer_8_out), .en(1'b1), .Q(cr), .clk(Clock));  // open: clr
  // Probe on cr
  and and_2 (jump, CQBool, comparator_8_eq);
  // Probe on jump
  and and_3 (link, CQBool, comparator_9_eq);
  Adder #(.width(24)) adder_1 (.a(Next_PC), .b(24'h1), .out(adder_1_out));  // open: cin, cout
  // Probe on Mem_Address
  Register #(.width(24)) register_3 (.D(multiplexer_9_out), .Q(Next_PC), .clk(Clock));  // open: en, clr
  Multiplexer #(.width(24), .enable("false")) multiplexer_9 (
    .in0(adder_1_out), .in1(IMM_VAL), .out(multiplexer_9_out), .sel(jump));
  not not_2 (not_2_out, or_6_out);
  or or_6 (or_6_out, CMP, not_3_out, JUMPLINK);
  not not_3 (not_3_out, CQBool);
  // Probe on multiplexer_10_out
  // Probe on Mem_Address
  RAM #(.addrWidth(24), .dataWidth(24), .bus("separate")) ram_2 (
    .addr(Mem_Address), .din(Mem_Data), .data(ram_2_data), .str(Mem_Write), .sel(not_2_out), .clk(Clock),
    .ld(comparator_10_eq));  // open: clr
  Comparator #(.width(4)) comparator_10 (.a(OP), .b(4'b1010), .eq(comparator_10_eq));  // open: gt, lt
  // Probe on ram_2_data
  Multiplexer #(.width(24), .enable("false")) multiplexer_10 (
    .in0(Mem_Address), .in1(ram_2_data), .out(multiplexer_10_out), .sel(comparator_10_eq));

  // Other names for the same wires on the sheet: clk = Clock; tunnel_t_t = cr[0]; tunnel_t = cr[1]; tunnel = cr[2];
  //   inst[31:0] = Instruction; memAddr[23:0] = Mem_Address; memData[23:0] = Mem_Data; memWrite = Mem_Write;
  //   nextPC[23:0] = Next_PC; oneA2RI[19:0] = oneA1RI[19:0]; oneA3RI[15:0] = oneA1RI[15:0];
  //   pipeline[31:0] = {OP, CQ, IMM, oneA1RI}; oneA3RS[3:0] = oneA1RI[19:16]; zeroA3RS[3:0] = oneA1RI[19:16];
  //   oneA2RD[3:0] = oneA1RI[23:20]; oneA3RD[3:0] = oneA1RI[23:20]; zeroA2RD[3:0] = oneA1RI[23:20];
  //   zeroA3RD[3:0] = oneA1RI[23:20]; TYPE[2:1] = {JUMPLINK, CMP}

  // Notes on the sheet:
  //   INPUTS
  //   INPUT PROBES
  //   OUTPUT PROBES
  //   OUTPUTS
  //   DO NOT MOVE/ADD/CHANGE ANY INPUT OR OUTPUT PINS!
endmodule
