// Logisim project REG.circ as structural Verilog: 1 circuit, main circuit Ida Register File
// Register File
module Ida_Register_File (
  input  [3:0] Read_Reg_1,
  input  [3:0] Read_Reg_2,
  input  [3:0] Write_Reg,
  input  [23:0] Write_Value,
  input  Reg_Write,
  input  Clock,
  output [23:0] Reg_1_Value,
  output [23:0] Reg_2_Value,
  output [23:0] Reg_3_Value,
  output [23:0] r00,
  output [23:0] r01,
  output [23:0] r02,
  output [23:0] r03,
  output [23:0] r04,
  output [23:0] r05,
  output [23:0] r06,
  output [23:0] r07,
  output [23:0] r08,
  output [23:0] r09,
  output [23:0] r10,
  output [23:0] r11,
  output [23:0] r12,
  output [23:0] r13,
  output [23:0] r14,
  output [23:0] r15
);

  wire D00, D01, D02, D03, D04, D05, D06, D07, D08, D09, D10, D11, D12, D13, D14, D15;
  wire [23:0] RR00, RR01, RR02, RR03, RR04, RR05, RR06, RR07, RR08, RR09, RR10, RR11, RR12, RR13, RR14, RR15;

  // Probe on Read_Reg_1
  // Probe on Read_Reg_2
  // Probe on Write_Reg
  // Probe on Write_Value
  // Probe on Reg_Write
  // Probe on Clock
  // Probe on Reg_1_Value
  // Probe on Reg_2_Value
  // Probe on Reg_3_Value
  // Probe on r00
  // Probe on r01
  // Probe on r02
  // Probe on r03
  // Probe on r04
  // Probe on r05
  // Probe on r06
  // Probe on r07
  // Probe on r08
  // Probe on r09
  // Probe on r10
  // Probe on r11
  // Probe on r12
  // Probe on r13
  // Probe on r14
  // Probe on r15
  Multiplexer #(.select(4), .width(24), .enable("false")) multiplexer_1 (
    .in0(r00), .in1(r01), .in2(r02), .in3(r03), .in4(r04), .in5(r05), .in6(r06), .in7(r07), .in8(r08),
    .in9(r09), .in10(r10), .in11(r11), .in12(r12), .in13(r13), .in14(r14), .in15(r15), .out(Reg_1_Value),
    .sel(Read_Reg_1));
  Multiplexer #(.select(4), .width(24), .enable("false")) multiplexer_2 (
    .in0(r00), .in1(r01), .in2(r02), .in3(r03), .in4(r04), .in5(r05), .in6(r06), .in7(r07), .in8(r08),
    .in9(r09), .in10(r10), .in11(r11), .in12(r12), .in13(r13), .in14(r14), .in15(r15), .out(Reg_3_Value),
    .sel(Write_Reg));
  Demultiplexer #(.select(4)) demultiplexer_1 (
    .out0(D00), .out1(D01), .out2(D02), .out3(D03), .out4(D04), .out5(D05), .out6(D06), .out7(D07),
    .out8(D08), .out9(D09), .out10(D10), .out11(D11), .out12(D12), .out13(D13), .out14(D14), .out15(D15),
    .in(1'b1), .sel(Write_Reg), .en(Reg_Write));
  Multiplexer #(.select(4), .width(24), .enable("false")) multiplexer_3 (
    .in0(r00), .in1(r01), .in2(r02), .in3(r03), .in4(r04), .in5(r05), .in6(r06), .in7(r07), .in8(r08),
    .in9(r09), .in10(r10), .in11(r11), .in12(r12), .in13(r13), .in14(r14), .in15(r15), .out(Reg_2_Value),
    .sel(Read_Reg_2));
  Demultiplexer #(.select(4), .width(24)) demultiplexer_2 (
    .out0(RR00), .out1(RR01), .out2(RR02), .out3(RR03), .out4(RR04), .out5(RR05), .out6(RR06), .out7(RR07),
    .out8(RR08), .out9(RR09), .out10(RR10), .out11(RR11), .out12(RR12), .out13(RR13), .out14(RR14),
    .out15(RR15), .in(Write_Value), .sel(Write_Reg), .en(Reg_Write));
  Register #(.width(24)) u_R00 (.D(RR00), .en(D00), .Q(r00), .clk(Clock));  // open: clr
  Register #(.width(24)) u_R01 (.D(RR01), .en(D01), .Q(r01), .clk(Clock));  // open: clr
  Register #(.width(24)) u_R02 (.D(RR02), .en(D02), .Q(r02), .clk(Clock));  // open: clr
  Register #(.width(24)) u_R03 (.D(RR03), .en(D03), .Q(r03), .clk(Clock));  // open: clr
  Register #(.width(24)) u_R04 (.D(RR04), .en(D04), .Q(r04), .clk(Clock));  // open: clr
  Register #(.width(24)) u_R05 (.D(RR05), .en(D05), .Q(r05), .clk(Clock));  // open: clr
  Register #(.width(24)) u_R06 (.D(RR06), .en(D06), .Q(r06), .clk(Clock));  // open: clr
  Register #(.width(24)) u_R07 (.D(RR07), .en(D07), .Q(r07), .clk(Clock));  // open: clr
  Register #(.width(24)) u_R08 (.D(RR08), .en(D08), .Q(r08), .clk(Clock));  // open: clr
  Register #(.width(24)) u_R09 (.D(RR09), .en(D09), .Q(r09), .clk(Clock));  // open: clr
  Register #(.width(24)) u_R10 (.D(RR10), .en(D10), .Q(r10), .clk(Clock));  // open: clr
  Register #(.width(24)) u_R11 (.D(RR11), .en(D11), .Q(r11), .clk(Clock));  // open: clr
  Register #(.width(24)) u_R12 (.D(RR12), .en(D12), .Q(r12), .clk(Clock));  // open: clr
  Register #(.width(24)) u_R13 (.D(RR13), .en(D13), .Q(r13), .clk(Clock));  // open: clr
  Register #(.width(24)) u_R14 (.D(RR14), .en(D14), .Q(r14), .clk(Clock));  // open: clr
  Register #(.width(24)) u_R15 (.D(RR15), .en(D15), .Q(r15), .clk(Clock));  // open: clr

  // Other names for the same wires on the sheet: clk = Clock; reg1Read[3:0] = Read_Reg_1; reg1Val[23:0] = Reg_1_Value;
  //   reg2Read[3:0] = Read_Reg_2; reg2Val[23:0] = Reg_2_Value; reg3Val[23:0] = Reg_3_Value;
  //   reg3Write[3:0] = Write_Reg; write = Reg_Write; writeVal[23:0] = Write_Value

  // Notes on the sheet:
  //   INPUT PINS
  //   INPUT PROBES
  //   OUTPUT PROBES
  //   OUTPUT PINS
  //   DO NOT MOVE/ADD/CHANGE ANY INPUT OR OUTPUT PINS!
endmodule
